// Logisim project освещение.circ as structural Verilog: 1 circuit, main circuit main
module main (
  input  \Перегрев ,
  input  \Ток_в_порядке ,
  input  \Перегрев_2 ,
  input  \датчик_Темно1 ,
  input  \Ток_в_порядке_2 ,
  input  \датчик_Темно2 ,
  input  \обнаружено_движение ,
  input  \Ключи_на_месте ,
  input  \Датчик_Темно1_2 ,
  input  \Включить_насильно ,
  input  \Датчик_Темно2_2 ,
  input  \Люди_дома_есть ,
  input  \включить_насильно_2 ,
  input  \Сосед_включил ,
  input  \Сосед_включил_2 
);

  wire and_1_out, and_2_out, and_3_out, and_4_out, not_1_out, not_2_out, or_1_out, or_2_out, or_3_out;

  not not_1 (not_1_out, \Перегрев_2 );
  or or_1 (or_1_out, \Датчик_Темно1_2 , \Датчик_Темно2_2 );
  and and_1 (and_1_out, \обнаружено_движение , or_1_out);
  or or_2 (or_2_out, and_1_out, \включить_насильно_2 , \Сосед_включил_2 );
  and and_2 (and_2_out, not_1_out, \Ток_в_порядке_2 , or_2_out);
  LED led_1 (.in(and_2_out));
  not not_2 (not_2_out, \Перегрев );
  and and_3 (and_3_out, \датчик_Темно1 , \датчик_Темно2 );
  or or_3 (or_3_out, \Ключи_на_месте , \Включить_насильно , \Люди_дома_есть , \Сосед_включил );
  and and_4 (and_4_out, not_2_out, \Ток_в_порядке , and_3_out, or_3_out);
  LED \u_свет_на_улице_ВКЛЮЧЕН  (.in(and_4_out));

  // Notes on the sheet:
  //   освещение в подъезде
endmodule
